// Logisim project homework1.circ as structural Verilog: 12 circuits, main circuit main
module main (
);

  wire ARMUX, Clk, FETCH, in1_in2_zero, IR_LD, MEM_LD, PC_INC, PC_LD, REG_LD, REG_MUX, ZF, ZF_LD;
  wire [11:0] adder_1_out, AddrOut, IR_OUT, pc_1_out_5;
  wire [15:0] ALU_RES, Din, R1, R2, R3, R4, R5, R6, R7, R8, REG_DATA, SRC_1, SRC_2;

  Clock clock_1 (.out(Clk));
  control_unit control_unit_1 (
    .IR_15_12(Din[15:12]), .IR_LD(IR_LD), .MEM_LD(MEM_LD), .REG_MUX(REG_MUX), .ZF_LD(ZF_LD), .REG_LD(REG_LD),
    .ARMUX(ARMUX), .PC_INC(PC_INC), .PC_LD(PC_LD), .FETCH(FETCH), .ZF(ZF), .Clk(Clk));
  alu in1_in2 (.i1(SRC_2), .i2(SRC_1), .Result(ALU_RES), .Zero(in1_in2_zero), .ALUOP(IR_OUT[11:6]));
  RAM #(.addrWidth(12), .dataWidth(16), .bus("separate")) ram_1 (
    .addr(AddrOut), .din(SRC_2), .data(Din), .str(MEM_LD), .sel(1'b1), .clk(Clk), .ld(1'b1));  // open: clr
  register_1 ZF_REG (.CLK(Clk), .Data(in1_in2_zero), .Load(ZF_LD), .Q(ZF));
  Adder #(.width(12)) adder_1 (.a(pc_1_out_5), .b(IR_OUT), .out(adder_1_out));  // open: cin, cout
  PC pc_1 (.Data(adder_1_out), .Load(PC_LD), .Clk(Clk), .Increment(PC_INC), .out_5(pc_1_out_5));
  Hex_Digit_Display hex_digit_display_1 (.value(R1[15:12]), .dp(1'b1));
  Hex_Digit_Display hex_digit_display_2 (.value(R1[11:8]), .dp(1'b1));
  instruction_register instruction_register_1 (.in_1(Din[11:0]), .IR_LD(IR_LD), .IR(IR_OUT), .Clk(Clk));
  Multiplexer #(.width(16), .enable("false")) multiplexer_1 (.in0(ALU_RES), .in1(Din), .out(REG_DATA), .sel(REG_MUX));
  Hex_Digit_Display hex_digit_display_3 (.value(R1[7:4]), .dp(1'b1));
  Hex_Digit_Display hex_digit_display_4 (.value(R1[3:0]), .dp(1'b1));
  Multiplexer #(.width(12), .enable("false")) multiplexer_2 (
    .in0(pc_1_out_5), .in1(SRC_1[11:0]), .out(AddrOut), .sel(ARMUX));
  register_bank register_bank_1 (
    .Data(REG_DATA), .Register_Select(IR_OUT[2:0]), .REG_LD(REG_LD), .Dout1(R1), .Dout2(R2), .Dout3(R3),
    .Dout4(R4), .Dout5(R5), .Dout6(R6), .Dout7(R7), .Dout8(R8), .Clk(Clk));
  Multiplexer #(.select(3), .width(16), .enable("false")) multiplexer_3 (
    .in0(R1), .in1(R2), .in2(R3), .in3(R4), .in4(R5), .in5(R6), .in6(R7), .in7(R8), .out(SRC_2),
    .sel(IR_OUT[8:6]));
  Multiplexer #(.select(3), .width(16), .enable("false")) multiplexer_4 (
    .in0(R1), .in1(R2), .in2(R3), .in3(R4), .in4(R5), .in5(R6), .in6(R7), .in7(R8), .out(SRC_1),
    .sel(IR_OUT[5:3]));

  // Other names for the same wires on the sheet: IR_IN[11:0] = Din[11:0]; Opcode[3:0] = Din[15:12];
  //   IR_OUT_2_0[2:0] = IR_OUT[2:0]; IR_OUT_5_3[2:0] = IR_OUT[5:3]; IR_OUT_8_6[2:0] = IR_OUT[8:6];
  //   IR_OUT_11_6[5:0] = IR_OUT[11:6]; IR_OUT_11_9[2:0] = IR_OUT[11:9]; SRC_1_11_0[11:0] = SRC_1[11:0]

  // Notes on the sheet:
  //   Hex Display
endmodule

module driver (
  input  [3:0] Qin,
  input  Pin,
  output a,
  output b,
  output p,
  output c,
  output d,
  output e,
  output f,
  output g
);

  wire and_1_out, and_2_out, and_3_out, and_4_out, and_5_out, and_6_out, and_7_out, and_8_out, and_9_out,
       and_10_out, and_11_out, and_12_out, and_13_out, and_14_out, and_15_out, and_16_out, not_1_out;

  and and_1 (and_1_out, ~Qin[0], ~Qin[2]);  // AND_Gate
  and and_2 (and_2_out, Qin[0], Qin[2]);
  and and_3 (and_3_out, Qin[1], Qin[0]);
  and and_4 (and_4_out, ~Qin[1], ~Qin[0]);  // AND_Gate
  and and_5 (and_5_out, ~Qin[2], ~Qin[0]);  // AND_Gate
  and and_6 (and_6_out, Qin[1], ~Qin[0]);  // AND_Gate
  and and_7 (and_7_out, ~Qin[2], Qin[1]);  // AND_Gate
  and and_8 (and_8_out, ~Qin[1], Qin[2], Qin[0]);  // AND_Gate
  and and_9 (and_9_out, ~Qin[2], ~Qin[0]);  // AND_Gate
  and and_10 (and_10_out, Qin[1], ~Qin[0]);  // AND_Gate
  and and_11 (and_11_out, ~Qin[1], ~Qin[0]);  // AND_Gate
  and and_12 (and_12_out, Qin[2], ~Qin[1]);  // AND_Gate
  and and_13 (and_13_out, Qin[2], ~Qin[0]);  // AND_Gate
  and and_14 (and_14_out, Qin[2], ~Qin[1]);  // AND_Gate
  and and_15 (and_15_out, ~Qin[2], Qin[1]);  // AND_Gate
  and and_16 (and_16_out, Qin[1], ~Qin[0]);  // AND_Gate
  or or_1 (a, and_1_out, and_2_out, Qin[1], Qin[3]);
  not not_1 (not_1_out, Qin[2]);
  or or_2 (b, not_1_out, and_3_out, and_4_out);
  or or_3 (c, Qin[2], Qin[0], ~Qin[1]);  // OR_Gate
  or or_4 (d, Qin[3], and_5_out, and_6_out, and_7_out, and_8_out);
  or or_5 (e, and_9_out, and_10_out);
  or or_6 (f, Qin[3], and_11_out, and_12_out, and_13_out);
  or or_7 (g, Qin[3], and_14_out, and_15_out, and_16_out);
  _7_Segment_Display u_7_segment_display_1 (.g(g), .f(f), .a(a), .b(b), .e(e), .d(d), .c(c), .dp(Pin));

  assign p = Pin;
endmodule

module register_1 (
  input  CLK,
  input  Data,
  input  Load,
  output Q
);

  wire and_1_out, and_2_out;

  and and_1 (and_1_out, Data, Load);
  and and_2 (and_2_out, ~Data, Load);  // AND_Gate
  S_R_Flip_Flop s_r_ff_1 (.S(and_1_out), .clk(CLK), .R(and_2_out), .Q(Q), .en(1'b1));  // open: Qn, preset, reset
endmodule

module register_4 (
  input  [3:0] Data,
  input  Load,
  input  Clk,
  output [3:0] Q
);

  register_1 register_1_1 (.CLK(Clk), .Data(Data[0]), .Load(Load), .Q(Q[0]));
  register_1 register_1_2 (.CLK(Clk), .Data(Data[1]), .Load(Load), .Q(Q[1]));
  register_1 register_1_3 (.CLK(Clk), .Data(Data[2]), .Load(Load), .Q(Q[2]));
  register_1 register_1_4 (.CLK(Clk), .Data(Data[3]), .Load(Load), .Q(Q[3]));
endmodule

module register_12 (
  input  [11:0] Data,
  input  Load,
  input  Clk,
  output [11:0] Q
);

  register_1 register_1_1 (.CLK(Clk), .Data(Data[0]), .Load(Load), .Q(Q[0]));
  register_1 register_1_2 (.CLK(Clk), .Data(Data[1]), .Load(Load), .Q(Q[1]));
  register_1 register_1_3 (.CLK(Clk), .Data(Data[2]), .Load(Load), .Q(Q[2]));
  register_1 register_1_4 (.CLK(Clk), .Data(Data[3]), .Load(Load), .Q(Q[3]));
  register_1 register_1_5 (.CLK(Clk), .Data(Data[4]), .Load(Load), .Q(Q[4]));
  register_1 register_1_6 (.CLK(Clk), .Data(Data[5]), .Load(Load), .Q(Q[5]));
  register_1 register_1_7 (.CLK(Clk), .Data(Data[6]), .Load(Load), .Q(Q[6]));
  register_1 register_1_8 (.CLK(Clk), .Data(Data[7]), .Load(Load), .Q(Q[7]));
  register_1 register_1_9 (.CLK(Clk), .Data(Data[8]), .Load(Load), .Q(Q[8]));
  register_1 register_1_10 (.CLK(Clk), .Data(Data[9]), .Load(Load), .Q(Q[9]));
  register_1 register_1_11 (.CLK(Clk), .Data(Data[10]), .Load(Load), .Q(Q[10]));
  register_1 register_1_12 (.CLK(Clk), .Data(Data[11]), .Load(Load), .Q(Q[11]));
endmodule

module register_16 (
  input  [15:0] Data,
  input  Load,
  input  Clk,
  output [15:0] Q
);

  register_1 register_1_1 (.CLK(Clk), .Data(Data[0]), .Load(Load), .Q(Q[0]));
  register_1 register_1_2 (.CLK(Clk), .Data(Data[1]), .Load(Load), .Q(Q[1]));
  register_1 register_1_3 (.CLK(Clk), .Data(Data[2]), .Load(Load), .Q(Q[2]));
  register_1 register_1_4 (.CLK(Clk), .Data(Data[3]), .Load(Load), .Q(Q[3]));
  register_1 register_1_5 (.CLK(Clk), .Data(Data[4]), .Load(Load), .Q(Q[4]));
  register_1 register_1_6 (.CLK(Clk), .Data(Data[5]), .Load(Load), .Q(Q[5]));
  register_1 register_1_7 (.CLK(Clk), .Data(Data[6]), .Load(Load), .Q(Q[6]));
  register_1 register_1_8 (.CLK(Clk), .Data(Data[7]), .Load(Load), .Q(Q[7]));
  register_1 register_1_9 (.CLK(Clk), .Data(Data[8]), .Load(Load), .Q(Q[8]));
  register_1 register_1_10 (.CLK(Clk), .Data(Data[9]), .Load(Load), .Q(Q[9]));
  register_1 register_1_11 (.CLK(Clk), .Data(Data[10]), .Load(Load), .Q(Q[10]));
  register_1 register_1_12 (.CLK(Clk), .Data(Data[11]), .Load(Load), .Q(Q[11]));
  register_1 register_1_13 (.CLK(Clk), .Data(Data[12]), .Load(Load), .Q(Q[12]));
  register_1 register_1_14 (.CLK(Clk), .Data(Data[13]), .Load(Load), .Q(Q[13]));
  register_1 register_1_15 (.CLK(Clk), .Data(Data[14]), .Load(Load), .Q(Q[14]));
  register_1 register_1_16 (.CLK(Clk), .Data(Data[15]), .Load(Load), .Q(Q[15]));
endmodule

module register_incdec (
  input  [15:0] Data,
  input  Load,
  input  Clk,
  input  Increment,
  input  Decrement,
  output [15:0] out_6
);

  wire not_1_out, or_1_out, or_2_out;
  wire [15:0] adder_1_out, multiplexer_1_out, multiplexer_2_out, subtractor_1_out;

  or or_1 (or_1_out, Increment, Decrement);
  Multiplexer #(.width(16), .enable("false")) multiplexer_1 (
    .in0(multiplexer_2_out), .in1(Data), .out(multiplexer_1_out), .sel(not_1_out));
  not not_1 (not_1_out, or_1_out);
  or or_2 (or_2_out, Load, or_1_out);
  register_16 register_16_1 (.Data(multiplexer_1_out), .Load(or_2_out), .Q(out_6), .Clk(Clk));
  Adder #(.width(16)) adder_1 (.a(16'h1), .b(out_6), .out(adder_1_out));  // open: cin, cout
  Multiplexer #(.width(16), .enable("false")) multiplexer_2 (
    .in0(adder_1_out), .in1(subtractor_1_out), .out(multiplexer_2_out), .sel(Decrement));
  Subtractor #(.width(16)) subtractor_1 (.a(out_6), .b(16'h1), .out(subtractor_1_out));  // open: bin, bout
endmodule

module register_bank (
  input  [15:0] Data,
  input  [2:0] Register_Select,
  input  REG_LD,
  input  Clk,
  output [15:0] Dout1,
  output [15:0] Dout2,
  output [15:0] Dout3,
  output [15:0] Dout4,
  output [15:0] Dout5,
  output [15:0] Dout6,
  output [15:0] Dout7,
  output [15:0] Dout8
);

  wire and_1_out, and_2_out, and_3_out, and_4_out, and_5_out, and_6_out, and_7_out, and_8_out,
       decoder_1_out0, decoder_1_out1, decoder_1_out2, decoder_1_out3, decoder_1_out4, decoder_1_out5,
       decoder_1_out6, decoder_1_out7;

  Decoder #(.select(3), .enable("false")) decoder_1 (
    .out0(decoder_1_out0), .out1(decoder_1_out1), .out2(decoder_1_out2), .out3(decoder_1_out3),
    .out4(decoder_1_out4), .out5(decoder_1_out5), .out6(decoder_1_out6), .out7(decoder_1_out7),
    .sel(Register_Select));
  and and_1 (and_1_out, decoder_1_out0, REG_LD);
  and and_2 (and_2_out, decoder_1_out1, REG_LD);
  and and_3 (and_3_out, decoder_1_out2, REG_LD);
  and and_4 (and_4_out, decoder_1_out3, REG_LD);
  and and_5 (and_5_out, decoder_1_out4, REG_LD);
  and and_6 (and_6_out, decoder_1_out5, REG_LD);
  and and_7 (and_7_out, decoder_1_out6, REG_LD);
  and and_8 (and_8_out, decoder_1_out7, REG_LD);
  register_16 register_16_1 (.Data(Data), .Load(and_1_out), .Q(Dout1), .Clk(Clk));
  register_16 register_16_2 (.Data(Data), .Load(and_2_out), .Q(Dout2), .Clk(Clk));
  register_16 register_16_3 (.Data(Data), .Load(and_3_out), .Q(Dout3), .Clk(Clk));
  register_16 register_16_4 (.Data(Data), .Load(and_4_out), .Q(Dout4), .Clk(Clk));
  register_16 register_16_5 (.Data(Data), .Load(and_5_out), .Q(Dout5), .Clk(Clk));
  register_16 register_16_6 (.Data(Data), .Load(and_6_out), .Q(Dout6), .Clk(Clk));
  register_16 register_16_7 (.Data(Data), .Load(and_7_out), .Q(Dout7), .Clk(Clk));
  register_16 register_16_8 (.Data(Data), .Load(and_8_out), .Q(Dout8), .Clk(Clk));
endmodule

module alu (
  input  [15:0] i1,
  input  [15:0] i2,
  input  [5:0] ALUOP,
  output [15:0] Result,
  output Zero
);

  wire [15:0] adder_1_out, adder_2_out, and_1_out, multiplexer_1_out, not_1_out, or_1_out, subtractor_1_out,
       subtractor_2_out, xor_1_out;

  Adder #(.width(16)) adder_1 (.a(i1), .b(i2), .out(adder_1_out));  // open: cin, cout
  Subtractor #(.width(16)) subtractor_1 (.a(i1), .b(i2), .out(subtractor_1_out));  // open: bin, bout
  assign and_1_out = i1 & i2;  // AND_Gate and_1, 16 bits wide
  assign or_1_out = i1 | i2;  // OR_Gate or_1, 16 bits wide
  assign xor_1_out = i1 ^ i2;  // XOR_Gate xor_1, 16 bits wide
  assign not_1_out = ~i2;  // NOT_Gate not_1, 16 bits wide
  Adder #(.width(16)) adder_2 (.a(i2), .b(16'h1), .out(adder_2_out));  // open: cin, cout
  Subtractor #(.width(16)) subtractor_2 (.a(i2), .b(16'h1), .out(subtractor_2_out));  // open: bin, bout
  Multiplexer #(.select(3), .width(16), .enable("false")) multiplexer_1 (
    .in0(not_1_out), .in1(i2), .in2(adder_2_out), .in3(subtractor_2_out), .in4({16{1'b0}}), .in5({16{1'b0}}),
    .in6({16{1'b0}}), .in7({16{1'b0}}), .out(multiplexer_1_out), .sel(ALUOP[2:0]));
  Multiplexer #(.select(3), .width(16), .enable("false")) multiplexer_2 (
    .in0(adder_1_out), .in1(subtractor_1_out), .in2(and_1_out), .in3(or_1_out), .in4(xor_1_out),
    .in5({16{1'b0}}), .in6({16{1'b0}}), .in7(multiplexer_1_out), .out(Result), .sel(ALUOP[5:3]));
  nor nor_1 (Zero, Result[15], Result[14], Result[13], Result[12], Result[11], Result[10], Result[9], Result[8], Result[7], Result[6], Result[5], Result[4], Result[3], Result[2], Result[1], Result[0]);
endmodule

module PC (
  input  [11:0] Data,
  input  Load,
  input  Clk,
  input  Increment,
  output [11:0] out_5
);

  wire not_1_out, or_1_out;
  wire [11:0] adder_1_out, multiplexer_1_out;

  Multiplexer #(.width(12), .enable("false")) multiplexer_1 (
    .in0(adder_1_out), .in1(Data), .out(multiplexer_1_out), .sel(not_1_out));
  or or_1 (or_1_out, Load, Increment);
  not not_1 (not_1_out, Increment);
  register_12 register_12_1 (.Data(multiplexer_1_out), .Load(or_1_out), .Clk(Clk), .Q(out_5));
  Adder #(.width(12)) adder_1 (.a(12'h1), .b(out_5), .out(adder_1_out));  // open: cin, cout
endmodule

module control_unit (
  input  [3:0] IR_15_12,
  input  ZF,
  input  Clk,
  output IR_LD,
  output MEM_LD,
  output REG_MUX,
  output ZF_LD,
  output REG_LD,
  output ARMUX,
  output PC_INC,
  output PC_LD,
  output FETCH
);

  wire [0:0] and_1_out;
  wire [3:0] multiplexer_1_out, multiplexer_2_out, register_4_1_q;

  and and_1 (and_1_out[0], ~IR_15_12[0], ~IR_15_12[1], IR_15_12[2], ~IR_15_12[3]);  // AND_Gate
  Multiplexer #(.select(2), .width(4), .enable("false")) multiplexer_1 (
    .in0(IR_15_12), .in1(IR_15_12), .in2(IR_15_12), .in3(4'b0101), .out(multiplexer_1_out),
    .sel({ZF, and_1_out[0]}));
  register_4 register_4_1 (.Data(multiplexer_2_out), .Load(1'b1), .Clk(Clk), .Q(register_4_1_q));
  Multiplexer #(.width(4), .enable("false")) multiplexer_2 (
    .in0(4'b0000), .in1(multiplexer_1_out), .out(multiplexer_2_out), .sel(FETCH));
  ROM #(.addrWidth(4), .dataWidth(9)) rom_1 (
    .addr(register_4_1_q), .data({FETCH, PC_LD, PC_INC, ARMUX, REG_LD, ZF_LD, REG_MUX, MEM_LD, IR_LD}),
    .sel(1'b1));

  // Notes on the sheet:
  //   contents of rom_1 (hex, n*v repeats v):
  //   141 54 34 22 0 80 0 18
endmodule

module instruction_register (
  input  [11:0] in_1,
  input  Clk,
  input  IR_LD,
  output [11:0] IR
);

  register_12 register_12_1 (.Data(in_1), .Load(IR_LD), .Clk(Clk), .Q(IR));
endmodule
